# Fritzing sketch rotaryEncoder (saved by Fritzing 0.9.3b)
breadboards: 1

parts:
  RE1 = Rotary Encoder [package=THT]
  Part3 = Arduino MKR1000
  R1 = Resistor [tolerance=±5% resistance=10k package="0805 [SMD]"]

nets:
  N1: RE1.EncoderPinA, Part3.D9_SCK
  N2: RE1.EncoderPinC, R1.Pin_1

custom parts:
  Arduino MKR1000: MKR1000 is a powerful board that combines the functionality of the Zero and the Wi-Fi Shield. It is the ideal solution for makers wanting to design IoT projects with minimal previous experience in networking
